# Fritzing sketch FTDI_Protoboard (saved by Fritzing 0.9.2b)
breadboards: 1

parts:
  Atmega1 = atmega328 [package=dip]
  S1 = Pushbutton [package="[THT]"]
  LED1 = smd LED [color="Red (633nm)" package="0603 [SMD]"]
  R1 = Resistor [tolerance=±5% resistance=220 package=THT]
  R2 = Resistor [tolerance=±5% resistance=10k package=THT]
  C2 = Ceramic Capacitor [capacitance=20pF voltage=6.3V package="100 mil [THT, multilayer]"]
  C3 = Ceramic Capacitor [capacitance=20pF voltage=6.3V package="100 mil [THT, multilayer]"]
  Y1 = CRYSTAL [package=hc49us]
  LED2 = LED - 5mm [color="Green (555nm)" package="5 mm [THT]"]
  R3 = Resistor [tolerance=±5% resistance=220 package=THT]
  Parte2 = FTDI Basic Programmer
  C4 = Ceramic Capacitor [capacitance=0.1µF package="100 mil [THT, multilayer]"]

nets:
  N1: Atmega1.RESET, S1.Pin_1, S1.Pin_2, R2.Pin_0, C4.1
  FTDI_TX: Atmega1.D0_(RX), Parte2.TXO
  FTDI_RX: Atmega1.D1_(TX), Parte2.RXI
  5V: Atmega1.VCC, Atmega1.AVCC, Atmega1.AREF, LED1.anode, R2.Pin_1, Parte2.POWER
  GND: Atmega1.GND, S1.Pin_3, S1.Pin_4, R1.Pin_1, C2.0, C3.1, R3.Pin_1, Parte2.CTS, Parte2.GND
  N2: Atmega1.XLAT1, C2.1, Y1.1
  N3: Atmega1.XLAT2, C3.0, Y1.2
  N4: Atmega1.D13, LED2.anode
  N5: LED1.cathode, R1.Pin_0
  N6: LED2.cathode, R3.Pin_0
  N7: Parte2.DTR, C4.0
