# Fritzing sketch RS232_Protoboard (saved by Fritzing 0.9.2b)
breadboards: 2

parts:
  U1 = RS232 Transceiver [package=dil16]
  C1 = Electrolytic Capacitor [capacitance=1µF package="100 mil [THT, electrolytic]"]
  C2 = Electrolytic Capacitor [capacitance=1µF package="100 mil [THT, electrolytic]"]
  C3 = Electrolytic Capacitor [capacitance=1µF package="100 mil [THT, electrolytic]"]
  C4 = Electrolytic Capacitor [capacitance=1µF package="100 mil [THT, electrolytic]"]
  X2 = DB9 Connector [package=db9]
  R1 = Resistor [tolerance=±5% resistance=1k package=THT]
  R2 = Resistor [tolerance=±5% resistance=1k package=THT]
  Atmega2 = atmega328 [package=dip]
  S2 = Pushbutton [package="[THT]"]
  LED3 = smd LED [color="Red (633nm)" package="0603 [SMD]"]
  R4 = Resistor [tolerance=±5% resistance=220 package=THT]
  R5 = Resistor [tolerance=±5% resistance=10k package=THT]
  C5 = Ceramic Capacitor [capacitance=20pF voltage=6.3V package="100 mil [THT, multilayer]"]
  C6 = Ceramic Capacitor [capacitance=20pF voltage=6.3V package="100 mil [THT, multilayer]"]
  Y2 = CRYSTAL [package=hc49us]
  LED4 = LED - 5mm [color="Green (555nm)" package="5 mm [THT]"]
  R6 = Resistor [tolerance=±5% resistance=220 package=THT]
  C7 = Ceramic Capacitor [capacitance=100nF package="100 mil [THT, multilayer]"]
  U2 = Voltage Regulator - 5V [package="TO220 [THT]"]
  VCC1 = Battery block 9V
  C8 = Electrolytic Capacitor [capacitance=10µF voltage=50V package="100 mil [THT, electrolytic]"]
  C9 = Electrolytic Capacitor [capacitance=10µF voltage=50V package="100 mil [THT, electrolytic]"]

nets:
  N1: U1.C1+, C1.+
  N2: U1.V+, C2.+
  N3: U1.C1-, C1.-
  N4: U1.C2+, C4.+
  N5: U1.C2-, C4.-
  N6: U1.V-, C3.+
  N7: U1.T2OUT, X2.2
  N8: U1.R2IN, X2.3
  N9: U1.R2OUT, R2.Pin_1
  N10: U1.T2IN, R1.Pin_1
  N11: U1.R1OUT, C7.0
  N12: U1.R1IN, X2.4
  GND: U1.GND, C2.-, C3.-, X2.5, Atmega2.GND, S2.Pin_3, S2.Pin_4, R4.Pin_1, C5.1, C6.0, R6.Pin_1, U2.GND, VCC1.-, C8.-, C9.-
  5V: U1.VCC, Atmega2.VCC, Atmega2.AVCC, Atmega2.AREF, LED3.anode, R5.Pin_1, U2.output_voltage, C9.+
  ATmega_TX: R1.Pin_0, Atmega2.D1_(TX)
  ATmega_RX: R2.Pin_0, Atmega2.D0_(RX)
  N13: Atmega2.RESET, S2.Pin_1, S2.Pin_2, R5.Pin_0, C7.1
  N14: Atmega2.XLAT1, C6.1, Y2.1
  N15: Atmega2.XLAT2, C5.0, Y2.2
  N16: Atmega2.D13, LED4.anode
  N17: LED3.cathode, R4.Pin_0
  N18: LED4.cathode, R6.Pin_0
  N19: U2.input_voltage, VCC1.+, C8.+

notes:
  Fuente de Poder
